// Logisim project atividade.circ as structural Verilog: 7 circuits, main circuit main
module main (
  input  [7:0] in_1,
  input  sMAR,
  input  eMAR,
  input  s1,
  input  s2,
  input  s3,
  input  s4,
  input  e1,
  input  e2,
  input  e3,
  input  e4,
  input  carry_in,
  input  [7:0] num1,
  input  [7:0] num2,
  output [7:0] out_15,
  output [7:0] result,
  output carry_out
);

  wire [7:0] MAR_out_4, registrador_8bits_1_out_4, registrador_8bits_2_out_4, registrador_8bits_3_out_4,
       registrador_8bits_4_out_4;

  // Probe on MAR_out_4
  registrador_8bits MAR (.in_1(in_1), .in_2(sMAR), .in_3(eMAR), .out_4(MAR_out_4));
  assign out_15 = eMAR ? MAR_out_4 : 8'bz;  // Controlled_Buffer controlled_buffer_1
  // Probe on registrador_8bits_1_out_4
  somador_8bits somador_8bits_1 (.in_1(carry_in), .in_2(num1), .in_3(num2), .out_4(result), .out_5(carry_out));
  assign out_15 = e1 ? registrador_8bits_1_out_4 : 8'bz;  // Controlled_Buffer controlled_buffer_2
  registrador_8bits registrador_8bits_1 (.in_1(out_15), .in_2(s1), .in_3(e1), .out_4(registrador_8bits_1_out_4));
  assign out_15 = e2 ? registrador_8bits_2_out_4 : 8'bz;  // Controlled_Buffer controlled_buffer_3
  // Probe on registrador_8bits_2_out_4
  registrador_8bits registrador_8bits_2 (.in_1(out_15), .in_2(s2), .in_3(e2), .out_4(registrador_8bits_2_out_4));
  assign out_15 = e3 ? registrador_8bits_3_out_4 : 8'bz;  // Controlled_Buffer controlled_buffer_4
  registrador_8bits registrador_8bits_3 (.in_1(out_15), .in_2(s3), .in_3(e3), .out_4(registrador_8bits_3_out_4));
  assign out_15 = e4 ? registrador_8bits_4_out_4 : 8'bz;  // Controlled_Buffer controlled_buffer_5
  registrador_8bits registrador_8bits_4 (.in_1(out_15), .in_2(s4), .in_3(e4), .out_4(registrador_8bits_4_out_4));
endmodule

module registrador_8bits (
  input  [7:0] in_1,
  input  in_2,
  input  in_3,
  output [7:0] out_4
);

  wire [7:0] memoria_um_bit_1_out_3;

  memoria_um_bit memoria_um_bit_1 (.in_1(in_1[0]), .in_2(in_2), .out_3(memoria_um_bit_1_out_3[0]));
  memoria_um_bit memoria_um_bit_2 (.in_1(in_1[1]), .in_2(in_2), .out_3(memoria_um_bit_1_out_3[1]));
  memoria_um_bit memoria_um_bit_3 (.in_1(in_1[2]), .in_2(in_2), .out_3(memoria_um_bit_1_out_3[2]));
  memoria_um_bit memoria_um_bit_4 (.in_1(in_1[3]), .in_2(in_2), .out_3(memoria_um_bit_1_out_3[3]));
  memoria_um_bit memoria_um_bit_5 (.in_1(in_1[4]), .in_2(in_2), .out_3(memoria_um_bit_1_out_3[4]));
  memoria_um_bit memoria_um_bit_6 (.in_1(in_1[5]), .in_2(in_2), .out_3(memoria_um_bit_1_out_3[5]));
  memoria_um_bit memoria_um_bit_7 (.in_1(in_1[6]), .in_2(in_2), .out_3(memoria_um_bit_1_out_3[6]));
  memoria_um_bit memoria_um_bit_8 (.in_1(in_1[7]), .in_2(in_2), .out_3(memoria_um_bit_1_out_3[7]));
  enable enable_1 (.in_1(memoria_um_bit_1_out_3), .in_2(in_3), .out_3(out_4));
endmodule

module memoria_um_bit (
  input  in_1,
  input  in_2,
  output out_3
);

  wire nand_1_out, nand_2_out, nand_4_out;

  nand nand_1 (nand_1_out, in_1, in_2);
  nand nand_2 (nand_2_out, nand_1_out, in_2);
  nand nand_3 (out_3, nand_1_out, nand_4_out);
  nand nand_4 (nand_4_out, out_3, nand_2_out);
endmodule

module registrador_2bits (
  input  in_1,
  input  in_2,
  input  in_3,
  output out_4,
  output out_5
);

  memoria_um_bit memoria_um_bit_1 (.in_1(in_1), .in_2(in_3), .out_3(out_4));
  memoria_um_bit memoria_um_bit_2 (.in_1(in_2), .in_2(in_3), .out_3(out_5));
endmodule

module enable (
  input  [7:0] in_1,
  input  in_2,
  output [7:0] out_3
);

  and and_1 (out_3[0], in_1[0], in_2);
  and and_2 (out_3[1], in_1[1], in_2);
  and and_3 (out_3[2], in_1[2], in_2);
  and and_4 (out_3[3], in_1[3], in_2);
  and and_5 (out_3[4], in_1[4], in_2);
  and and_6 (out_3[5], in_1[5], in_2);
  and and_7 (out_3[6], in_1[6], in_2);
  and and_8 (out_3[7], in_1[7], in_2);
endmodule

module somador1 (
  input  in_1,
  input  in_2,
  input  in_3,
  output out_4,
  output out_5
);

  wire and_1_out, and_2_out, and_3_out, xor_1_out;

  xor xor_1 (xor_1_out, in_1, in_2);
  and and_1 (and_1_out, in_2, in_3);
  and and_2 (and_2_out, in_2, in_1);
  and and_3 (and_3_out, in_3, in_1);
  xor xor_2 (out_4, xor_1_out, in_3);
  or or_1 (out_5, and_1_out, and_2_out, and_3_out);
endmodule

module somador_8bits (
  input  in_1,
  input  [7:0] in_2,
  input  [7:0] in_3,
  output [7:0] out_4,
  output out_5
);

  wire somador1_1_out_5, somador1_2_out_5, somador1_3_out_5, somador1_4_out_5, somador1_5_out_5,
       somador1_6_out_5, somador1_7_out_5;

  somador1 somador1_1 (.in_2(in_2[0]), .in_3(in_3[0]), .in_1(in_1), .out_4(out_4[0]), .out_5(somador1_1_out_5));
  somador1 somador1_2 (
    .in_2(in_2[1]), .in_3(in_3[1]), .in_1(somador1_1_out_5), .out_4(out_4[1]), .out_5(somador1_2_out_5));
  somador1 somador1_3 (
    .in_2(in_2[2]), .in_3(in_3[2]), .in_1(somador1_2_out_5), .out_4(out_4[2]), .out_5(somador1_3_out_5));
  somador1 somador1_4 (
    .in_2(in_2[3]), .in_3(in_3[3]), .in_1(somador1_3_out_5), .out_4(out_4[3]), .out_5(somador1_4_out_5));
  somador1 somador1_5 (
    .in_2(in_2[4]), .in_3(in_3[4]), .in_1(somador1_4_out_5), .out_4(out_4[4]), .out_5(somador1_5_out_5));
  somador1 somador1_6 (
    .in_2(in_2[5]), .in_3(in_3[5]), .in_1(somador1_5_out_5), .out_4(out_4[5]), .out_5(somador1_6_out_5));
  somador1 somador1_7 (
    .in_2(in_2[6]), .in_3(in_3[6]), .in_1(somador1_6_out_5), .out_4(out_4[6]), .out_5(somador1_7_out_5));
  somador1 somador1_8 (.in_2(in_2[7]), .in_3(in_3[7]), .in_1(somador1_7_out_5), .out_4(out_4[7]), .out_5(out_5));
endmodule
