// Logisim project atividade2.circ as structural Verilog: 12 circuits, main circuit main
module main (
  input  in_1,
  input  [7:0] in_2,
  input  in_3,
  input  in_4,
  input  in_5,
  input  in_6,
  input  in_7,
  input  in_8,
  input  in_9,
  input  in_10,
  input  in_11,
  input  in_12,
  input  in_13
);

  wire or_1_out;
  wire [7:0] controlled_buffer_1_out, mar_q;

  assign controlled_buffer_1_out = in_3 ? in_2 : 8'bz;  // Controlled_Buffer controlled_buffer_1
  // Probe on controlled_buffer_1_out
  registrador R1 (.in_1(controlled_buffer_1_out), .in_2(in_9), .in_3(in_10), .out_4(controlled_buffer_1_out));
  registrador R2 (.in_1(controlled_buffer_1_out), .in_2(in_11), .in_3(in_12), .out_4(controlled_buffer_1_out));
  registrador R3 (.in_1(controlled_buffer_1_out), .in_2(in_5), .in_3(in_6), .out_4(controlled_buffer_1_out));
  registrador R4 (.in_1(controlled_buffer_1_out), .in_2(in_7), .in_3(in_8), .out_4(controlled_buffer_1_out));
  Register mar (.D(controlled_buffer_1_out), .Q(mar_q), .clk(in_1));  // open: en, clr
  or or_1 (or_1_out, in_4, in_13);
  RAM #(.databus("bidir")) ram_1 (.addr(mar_q), .we(in_4), .oe(in_13), .clk(or_1_out));  // open: data

  // Notes on the sheet:
  //   22400829-Michael Willian Pereira Vieira
endmodule

module memoria_8bits (
  input  [7:0] in_1,
  input  in_2,
  output [7:0] out_3
);

  memoria_um_bit memoria_um_bit_1 (.in_1(in_1[0]), .in_2(in_2), .out_3(out_3[0]));
  memoria_um_bit memoria_um_bit_2 (.in_1(in_1[1]), .in_2(in_2), .out_3(out_3[1]));
  memoria_um_bit memoria_um_bit_3 (.in_1(in_1[2]), .in_2(in_2), .out_3(out_3[2]));
  memoria_um_bit memoria_um_bit_4 (.in_1(in_1[3]), .in_2(in_2), .out_3(out_3[3]));
  memoria_um_bit memoria_um_bit_5 (.in_1(in_1[4]), .in_2(in_2), .out_3(out_3[4]));
  memoria_um_bit memoria_um_bit_6 (.in_1(in_1[5]), .in_2(in_2), .out_3(out_3[5]));
  memoria_um_bit memoria_um_bit_7 (.in_1(in_1[6]), .in_2(in_2), .out_3(out_3[6]));
  memoria_um_bit memoria_um_bit_8 (.in_1(in_1[7]), .in_2(in_2), .out_3(out_3[7]));
endmodule

module memoria_um_bit (
  input  in_1,
  input  in_2,
  output out_3
);

  wire nand_1_out, nand_2_out, nand_4_out;

  nand nand_1 (nand_1_out, in_1, in_2);
  nand nand_2 (nand_2_out, nand_1_out, in_2);
  nand nand_3 (out_3, nand_1_out, nand_4_out);
  nand nand_4 (nand_4_out, out_3, nand_2_out);
endmodule

module enable (
  input  [7:0] in_1,
  input  in_2,
  output [7:0] out_3
);

  wire [7:0] and_1_out;

  and and_1 (and_1_out[0], in_1[0], in_2);
  and and_2 (and_1_out[1], in_1[1], in_2);
  and and_3 (and_1_out[2], in_1[2], in_2);
  and and_4 (and_1_out[3], in_1[3], in_2);
  and and_5 (and_1_out[4], in_1[4], in_2);
  and and_6 (and_1_out[5], in_1[5], in_2);
  and and_7 (and_1_out[6], in_1[6], in_2);
  and and_8 (and_1_out[7], in_1[7], in_2);
  assign out_3 = in_2 ? and_1_out : 8'bz;  // Controlled_Buffer controlled_buffer_1
endmodule

module deco_2x4 (
  input  in_1,
  input  in_2,
  output out_3,
  output out_4,
  output out_5,
  output out_6
);

  wire not_1_out, not_2_out;

  not not_1 (not_1_out, in_1);
  not not_2 (not_2_out, in_2);
  and and_1 (out_3, not_1_out, not_2_out);
  and and_2 (out_4, not_2_out, in_1);
  and and_3 (out_5, not_1_out, in_2);
  and and_4 (out_6, in_1, in_2);
endmodule

module registrador (
  input  [7:0] in_1,
  input  in_2,
  input  in_3,
  output [7:0] out_4
);

  wire [7:0] memoria_um_bit_1_out_3;

  memoria_um_bit memoria_um_bit_1 (.in_1(in_1[0]), .in_2(in_2), .out_3(memoria_um_bit_1_out_3[0]));
  memoria_um_bit memoria_um_bit_2 (.in_1(in_1[1]), .in_2(in_2), .out_3(memoria_um_bit_1_out_3[1]));
  memoria_um_bit memoria_um_bit_3 (.in_1(in_1[2]), .in_2(in_2), .out_3(memoria_um_bit_1_out_3[2]));
  memoria_um_bit memoria_um_bit_4 (.in_1(in_1[3]), .in_2(in_2), .out_3(memoria_um_bit_1_out_3[3]));
  memoria_um_bit memoria_um_bit_5 (.in_1(in_1[4]), .in_2(in_2), .out_3(memoria_um_bit_1_out_3[4]));
  memoria_um_bit memoria_um_bit_6 (.in_1(in_1[5]), .in_2(in_2), .out_3(memoria_um_bit_1_out_3[5]));
  memoria_um_bit memoria_um_bit_7 (.in_1(in_1[6]), .in_2(in_2), .out_3(memoria_um_bit_1_out_3[6]));
  memoria_um_bit memoria_um_bit_8 (.in_1(in_1[7]), .in_2(in_2), .out_3(memoria_um_bit_1_out_3[7]));
  assign out_4 = in_3 ? memoria_um_bit_1_out_3 : 8'bz;  // Controlled_Buffer controlled_buffer_1
endmodule

module ramAula3 (
  input  [7:0] in_1,
  input  in_2,
  input  in_3,
  input  in_4,
  input  [7:0] in_5,
  input  in_6,
  input  in_7,
  input  in_8,
  input  in_9
);

  wire or_1_out;
  wire [7:0] mar_q, registrador_1_out_4;

  // Probe on registrador_1_out_4
  registrador registrador_1 (.in_1(in_1), .in_2(in_3), .in_3(in_4), .out_4(registrador_1_out_4));
  registrador registrador_2 (.in_1(in_5), .in_2(in_6), .in_3(in_7), .out_4(registrador_1_out_4));
  or or_1 (or_1_out, in_8, in_9);
  Register mar (.D(registrador_1_out_4), .Q(mar_q), .clk(in_2));  // open: en, clr
  RAM #(.databus("bidir")) ram_1 (.addr(mar_q), .we(in_8), .oe(in_9), .clk(or_1_out));  // open: data
endmodule

module shift_l (
  input  car_in,
  input  [7:0] in_2,
  output [7:0] out_3,
  output car_out
);


  assign car_out = in_2[7];
  assign out_3 = {in_2[6:0], car_in};
endmodule

module shift_r (
  input  [7:0] in_1,
  input  car_in,
  output [7:0] out_3,
  output car_out
);


  assign car_out = in_1[0];
  assign out_3 = {car_in, in_1[7:1]};
endmodule

module ULA (
  input  [7:0] A,
  input  [7:0] B,
  input  c_in,
  input  in_4,
  input  in_5,
  output [7:0] out_6,
  output c_out,
  output [7:0] out_8,
  output out_9,
  output [7:0] out_10,
  output out_11
);

  somador8 somador8_1 (.in_1(c_in), .in_2(B), .in_3(A), .out_4(out_6), .out_5(c_out));
  shift_r sr (.in_1(A), .car_in(in_4), .out_3(out_8), .car_out(out_9));
  shift_l sl (.car_in(in_5), .in_2(A), .out_3(out_10), .car_out(out_11));
endmodule

module somador1 (
  input  in_1,
  input  in_2,
  input  in_3,
  output out_4,
  output out_5
);

  wire and_1_out, and_2_out, and_3_out, xor_1_out;

  xor xor_1 (xor_1_out, in_1, in_2);
  and and_1 (and_1_out, in_2, in_3);
  and and_2 (and_2_out, in_2, in_1);
  and and_3 (and_3_out, in_3, in_1);
  xor xor_2 (out_4, xor_1_out, in_3);
  or or_1 (out_5, and_1_out, and_2_out, and_3_out);
endmodule

module somador8 (
  input  in_1,
  input  [7:0] in_2,
  input  [7:0] in_3,
  output [7:0] out_4,
  output out_5
);

  wire somador1_1_out_5, somador1_2_out_5, somador1_3_out_5, somador1_4_out_5, somador1_5_out_5,
       somador1_6_out_5, somador1_7_out_5;

  somador1 somador1_1 (.in_2(in_2[0]), .in_3(in_3[0]), .in_1(in_1), .out_4(out_4[0]), .out_5(somador1_1_out_5));
  somador1 somador1_2 (
    .in_2(in_2[1]), .in_3(in_3[1]), .in_1(somador1_1_out_5), .out_4(out_4[1]), .out_5(somador1_2_out_5));
  somador1 somador1_3 (
    .in_2(in_2[2]), .in_3(in_3[2]), .in_1(somador1_2_out_5), .out_4(out_4[2]), .out_5(somador1_3_out_5));
  somador1 somador1_4 (
    .in_2(in_2[3]), .in_3(in_3[3]), .in_1(somador1_3_out_5), .out_4(out_4[3]), .out_5(somador1_4_out_5));
  somador1 somador1_5 (
    .in_2(in_2[4]), .in_3(in_3[4]), .in_1(somador1_4_out_5), .out_4(out_4[4]), .out_5(somador1_5_out_5));
  somador1 somador1_6 (
    .in_2(in_2[5]), .in_3(in_3[5]), .in_1(somador1_5_out_5), .out_4(out_4[5]), .out_5(somador1_6_out_5));
  somador1 somador1_7 (
    .in_2(in_2[6]), .in_3(in_3[6]), .in_1(somador1_6_out_5), .out_4(out_4[6]), .out_5(somador1_7_out_5));
  somador1 somador1_8 (.in_2(in_2[7]), .in_3(in_3[7]), .in_1(somador1_7_out_5), .out_4(out_4[7]), .out_5(out_5));
endmodule
