// Logisim project atividade3.circ as structural Verilog: 7 circuits, main circuit main
module main (
  input  enamar,
  input  enatmp,
  input  write,
  input  [2:0] in_4,
  input  set1,
  input  set2,
  input  set3,
  input  set4,
  input  output_ram,
  input  ena1,
  input  ena2,
  input  ena3,
  input  ena4,
  input  setacc,
  input  enaacc,
  output carry_out,
  output A_larger_than_b,
  output A_equal_B,
  output zero
);

  wire or_1_out;
  wire [7:0] acc_q, controlled_buffer_1_out, mar_q, R1_q, R2_q, R3_q, R4_q, tmp_q, ulalau_out_5;

  ULA ulalau (
    .A(controlled_buffer_1_out), .B(tmp_q), .out_5(ulalau_out_5), .in_1(in_4), .carry_out(carry_out),
    .A_larger_than_B(A_larger_than_b), .A_equal_B(A_equal_B), .zero(zero));
  Register tmp (.D(controlled_buffer_1_out), .Q(tmp_q), .clk(enatmp));  // open: en, clr
  Register acc (.D(ulalau_out_5), .Q(acc_q), .clk(setacc));  // open: en, clr
  assign controlled_buffer_1_out = enaacc ? acc_q : 8'bz;  // Controlled_Buffer controlled_buffer_1
  assign controlled_buffer_1_out = ena1 ? R1_q : 8'bz;  // Controlled_Buffer controlled_buffer_2
  Register R1 (.D(controlled_buffer_1_out), .Q(R1_q), .clk(set1));  // open: en, clr
  assign controlled_buffer_1_out = ena2 ? R2_q : 8'bz;  // Controlled_Buffer controlled_buffer_3
  Register R2 (.D(controlled_buffer_1_out), .Q(R2_q), .clk(set2));  // open: en, clr
  Register R3 (.D(controlled_buffer_1_out), .Q(R3_q), .clk(set3));  // open: en, clr
  assign controlled_buffer_1_out = ena3 ? R3_q : 8'bz;  // Controlled_Buffer controlled_buffer_4
  assign controlled_buffer_1_out = ena4 ? R4_q : 8'bz;  // Controlled_Buffer controlled_buffer_5
  Register R4 (.D(controlled_buffer_1_out), .Q(R4_q), .clk(set4));  // open: en, clr
  or or_1 (or_1_out, write, output_ram);
  Register mar (.D(controlled_buffer_1_out), .Q(mar_q), .clk(enamar));  // open: en, clr
  RAM #(.databus("bidir")) ram_1 (.addr(mar_q), .we(write), .oe(output_ram), .clk(or_1_out));  // open: data

  // Notes on the sheet:
  //   22400829-Michael_Willian_Pereira_Vieira
endmodule

module somador1 (
  input  in_1,
  input  in_2,
  input  in_3,
  output out_4,
  output out_5
);

  wire and_1_out, and_2_out, and_3_out, xor_1_out;

  xor xor_1 (xor_1_out, in_1, in_2);
  and and_1 (and_1_out, in_2, in_3);
  and and_2 (and_2_out, in_2, in_1);
  and and_3 (and_3_out, in_3, in_1);
  xor xor_2 (out_4, xor_1_out, in_3);
  or or_1 (out_5, and_1_out, and_2_out, and_3_out);
endmodule

module somador8 (
  input  in_1,
  input  [7:0] in_2,
  input  [7:0] in_3,
  output [7:0] out_4,
  output out_5
);

  wire somador1_1_out_5, somador1_2_out_5, somador1_3_out_5, somador1_4_out_5, somador1_5_out_5,
       somador1_6_out_5, somador1_7_out_5;

  somador1 somador1_1 (.in_2(in_2[0]), .in_3(in_3[0]), .in_1(in_1), .out_4(out_4[0]), .out_5(somador1_1_out_5));
  somador1 somador1_2 (
    .in_2(in_2[1]), .in_3(in_3[1]), .in_1(somador1_1_out_5), .out_4(out_4[1]), .out_5(somador1_2_out_5));
  somador1 somador1_3 (
    .in_2(in_2[2]), .in_3(in_3[2]), .in_1(somador1_2_out_5), .out_4(out_4[2]), .out_5(somador1_3_out_5));
  somador1 somador1_4 (
    .in_2(in_2[3]), .in_3(in_3[3]), .in_1(somador1_3_out_5), .out_4(out_4[3]), .out_5(somador1_4_out_5));
  somador1 somador1_5 (
    .in_2(in_2[4]), .in_3(in_3[4]), .in_1(somador1_4_out_5), .out_4(out_4[4]), .out_5(somador1_5_out_5));
  somador1 somador1_6 (
    .in_2(in_2[5]), .in_3(in_3[5]), .in_1(somador1_5_out_5), .out_4(out_4[5]), .out_5(somador1_6_out_5));
  somador1 somador1_7 (
    .in_2(in_2[6]), .in_3(in_3[6]), .in_1(somador1_6_out_5), .out_4(out_4[6]), .out_5(somador1_7_out_5));
  somador1 somador1_8 (.in_2(in_2[7]), .in_3(in_3[7]), .in_1(somador1_7_out_5), .out_4(out_4[7]), .out_5(out_5));
endmodule

module shift_r (
  input  [7:0] in_1,
  input  car_in,
  output [7:0] out_3,
  output car_out
);


  assign car_out = in_1[0];
  assign out_3 = {car_in, in_1[7:1]};
endmodule

module shift_l (
  input  car_in,
  input  [7:0] in_2,
  output [7:0] out_3,
  output car_out
);


  assign car_out = in_2[7];
  assign out_3 = {in_2[6:0], car_in};
endmodule

module ULA (
  input  [2:0] in_1,
  input  [7:0] A,
  input  [7:0] B,
  output carry_out,
  output [7:0] out_5,
  output A_larger_than_B,
  output A_equal_B,
  output zero
);

  wire sl_car_out, somador_8bits_out_5, sr_car_out;
  wire [7:0] Porta_and_out, Porta_not_out, Porta_or_out, Porta_xor_out, sl_out_3, somador_8bits_out_4,
       sr_out_3;

  somador8 somador_8bits (.in_1(1'b0), .in_2(B), .in_3(A), .out_4(somador_8bits_out_4), .out_5(somador_8bits_out_5));
  shift_r sr (.in_1(A), .car_in(1'b0), .out_3(sr_out_3), .car_out(sr_car_out));
  shift_l sl (.car_in(1'b0), .in_2(A), .out_3(sl_out_3), .car_out(sl_car_out));
  assign Porta_not_out = ~A;  // NOT_Gate Porta_not, 8 bits wide
  assign Porta_and_out = B & A;  // AND_Gate Porta_and, 8 bits wide
  assign Porta_or_out = B | A;  // OR_Gate Porta_or, 8 bits wide
  assign Porta_xor_out = B ^ A;  // XOR_Gate Porta_xor, 8 bits wide
  Comparator comparator_1 (.a(A), .b(B), .gt(A_larger_than_B), .eq(A_equal_B));  // open: lt
  Multiplexer #(.select(3)) multiplexer_1 (
    .in0(somador_8bits_out_5), .in1(sr_car_out), .in2(sl_car_out), .in3(1'b0), .in4(1'b0), .in5(1'b0),
    .in6(1'b0), .in7(1'b0), .out(carry_out), .sel(in_1));
  Multiplexer #(.select(3), .width(8)) multiplexer_2 (
    .in0(somador_8bits_out_4), .in1(sr_out_3), .in2(sl_out_3), .in3(Porta_not_out), .in4(Porta_and_out),
    .in5(Porta_or_out), .in6(Porta_xor_out), .in7(A), .out(out_5), .sel(in_1));
  nor nor_1 (zero, out_5[0], out_5[1], out_5[2], out_5[3], out_5[4], out_5[5], out_5[6], out_5[7]);
endmodule

module ramAula3 (
  input  enamar,
  input  enatmp,
  input  write,
  input  [2:0] in_4,
  input  set1,
  input  set2,
  input  set3,
  input  set4,
  input  output_ram,
  input  ena1,
  input  ena2,
  input  ena3,
  input  ena4,
  input  setacc,
  input  enaacc,
  output carry_out,
  output A_larger_than_b,
  output A_equal_B,
  output zero
);

  wire or_1_out;
  wire [7:0] acc_q, controlled_buffer_1_out, mar_q, R1_q, R2_q, R3_q, R4_q, tmp_q, ulalau_out_5;

  ULA ulalau (
    .A(controlled_buffer_1_out), .B(tmp_q), .out_5(ulalau_out_5), .in_1(in_4), .carry_out(carry_out),
    .A_larger_than_B(A_larger_than_b), .A_equal_B(A_equal_B), .zero(zero));
  Register tmp (.D(controlled_buffer_1_out), .Q(tmp_q), .clk(enatmp));  // open: en, clr
  Register acc (.D(ulalau_out_5), .Q(acc_q), .clk(setacc));  // open: en, clr
  assign controlled_buffer_1_out = enaacc ? acc_q : 8'bz;  // Controlled_Buffer controlled_buffer_1
  assign controlled_buffer_1_out = ena1 ? R1_q : 8'bz;  // Controlled_Buffer controlled_buffer_2
  Register R1 (.D(controlled_buffer_1_out), .Q(R1_q), .clk(set1));  // open: en, clr
  assign controlled_buffer_1_out = ena2 ? R2_q : 8'bz;  // Controlled_Buffer controlled_buffer_3
  Register R2 (.D(controlled_buffer_1_out), .Q(R2_q), .clk(set2));  // open: en, clr
  Register R3 (.D(controlled_buffer_1_out), .Q(R3_q), .clk(set3));  // open: en, clr
  assign controlled_buffer_1_out = ena3 ? R3_q : 8'bz;  // Controlled_Buffer controlled_buffer_4
  assign controlled_buffer_1_out = ena4 ? R4_q : 8'bz;  // Controlled_Buffer controlled_buffer_5
  Register R4 (.D(controlled_buffer_1_out), .Q(R4_q), .clk(set4));  // open: en, clr
  or or_1 (or_1_out, write, output_ram);
  Register mar (.D(controlled_buffer_1_out), .Q(mar_q), .clk(enamar));  // open: en, clr
  RAM #(.databus("bidir")) ram_1 (.addr(mar_q), .we(write), .oe(output_ram), .clk(or_1_out));  // open: data

  // Notes on the sheet:
  //   22400829-Michael_Willian_Pereira_Vieira
endmodule
