// Logisim project aula 1.circ as structural Verilog
module main (
  input  [7:0] in_1,
  input  [7:0] in_2,
  input  in_3,
  input  in_4,
  input  in_5,
  output [7:0] out_6,
  output out_7,
  output out_8
);

  somador1 somador1_1 ();  // open: in_2, in_3, in_1, out_4, out_5
  somador somador_1 (.in_1(in_1), .in_2(in_2), .out_3(out_6));
  somador1 somador1_2 (.in_2(in_4), .in_3(in_5), .in_1(in_3), .out_4(out_7), .out_5(out_7));

  assign out_8 = out_7;
endmodule

module somador (
  input  [7:0] in_1,
  input  [7:0] in_2,
  output [7:0] out_3
);
endmodule

module somador1 (
  input  in_1,
  input  in_2,
  input  in_3,
  output out_4,
  output out_5
);

  wire and_1_out, and_2_out, and_3_out, xor_1_out;

  xor xor_1 (xor_1_out, in_2, in_1);
  and and_1 (and_1_out, in_2, in_1);
  and and_2 (and_2_out, in_2, in_1);
  and and_3 (and_3_out, in_1, in_1);
  xor xor_2 (out_4, xor_1_out, in_1);
  or or_1 (out_5, and_1_out, and_2_out, and_3_out);

  assign in_3 = in_1;
endmodule

module meioSomador (
  input  in_1,
  input  in_2,
  output out_3,
  output out_4
);
endmodule
