// Logisim project aula1.circ as structural Verilog: 3 circuits, main circuit somador8
module main (
  input  in_1,
  input  [7:0] num1,
  input  [7:0] num2,
  output [7:0] result,
  output carry
);

  somador8 somador8_1 (.in_1(in_1), .in_2(num1), .in_3(num2), .out_4(result), .out_5(carry));
endmodule

module somador8 (
  input  in_1,
  input  [7:0] in_2,
  input  [7:0] in_3,
  output [7:0] out_4,
  output out_5
);

  wire somador1_1_out_5, somador1_2_out_5, somador1_3_out_5, somador1_4_out_5, somador1_5_out_5,
       somador1_6_out_5, somador1_7_out_5;

  somador1 somador1_1 (.in_2(in_2[0]), .in_3(in_3[0]), .in_1(in_1), .out_4(out_4[0]), .out_5(somador1_1_out_5));
  somador1 somador1_2 (
    .in_2(in_2[1]), .in_3(in_3[1]), .in_1(somador1_1_out_5), .out_4(out_4[1]), .out_5(somador1_2_out_5));
  somador1 somador1_3 (
    .in_2(in_2[2]), .in_3(in_3[2]), .in_1(somador1_2_out_5), .out_4(out_4[2]), .out_5(somador1_3_out_5));
  somador1 somador1_4 (
    .in_2(in_2[3]), .in_3(in_3[3]), .in_1(somador1_3_out_5), .out_4(out_4[3]), .out_5(somador1_4_out_5));
  somador1 somador1_5 (
    .in_2(in_2[4]), .in_3(in_3[4]), .in_1(somador1_4_out_5), .out_4(out_4[4]), .out_5(somador1_5_out_5));
  somador1 somador1_6 (
    .in_2(in_2[5]), .in_3(in_3[5]), .in_1(somador1_5_out_5), .out_4(out_4[5]), .out_5(somador1_6_out_5));
  somador1 somador1_7 (
    .in_2(in_2[6]), .in_3(in_3[6]), .in_1(somador1_6_out_5), .out_4(out_4[6]), .out_5(somador1_7_out_5));
  somador1 somador1_8 (.in_2(in_2[7]), .in_3(in_3[7]), .in_1(somador1_7_out_5), .out_4(out_4[7]), .out_5(out_5));
endmodule

module somador1 (
  input  in_1,
  input  in_2,
  input  in_3,
  output out_4,
  output out_5
);

  wire and_1_out, and_2_out, and_3_out, xor_1_out;

  xor xor_1 (xor_1_out, in_1, in_2);
  and and_1 (and_1_out, in_2, in_3);
  and and_2 (and_2_out, in_2, in_1);
  and and_3 (and_3_out, in_3, in_1);
  xor xor_2 (out_4, xor_1_out, in_3);
  or or_1 (out_5, and_1_out, and_2_out, and_3_out);
endmodule
