// Logisim project aula2.circ as structural Verilog: 5 circuits, main circuit main
module main (
  input  [7:0] input1,
  input  [7:0] in_2,
  input  [7:0] in_3,
  input  set,
  input  in_5,
  input  in_6,
  input  in_7,
  input  in_8,
  input  in_9,
  output [7:0] out_10
);

  wire [7:0] registrador_8bits_1_out_3, registrador_8bits_2_out_3, registrador_8bits_3_out_3;

  // Probe on out_10
  // Probe on registrador_8bits_1_out_3
  registrador_8bits registrador_8bits_1 (.in_1(input1), .in_2(set), .out_3(registrador_8bits_1_out_3));
  enable enable_1 (.in_1(registrador_8bits_1_out_3), .in_2(in_7), .out_3(out_10));
  enable enable_2 (.in_1(registrador_8bits_2_out_3), .in_2(in_8), .out_3(out_10));
  registrador_8bits registrador_8bits_2 (.in_1(in_2), .in_2(in_5), .out_3(registrador_8bits_2_out_3));
  enable enable_3 (.in_1(registrador_8bits_3_out_3), .in_2(in_9), .out_3(out_10));
  registrador_8bits registrador_8bits_3 (.in_1(in_3), .in_2(in_6), .out_3(registrador_8bits_3_out_3));
endmodule

module registrador_8bits (
  input  [7:0] in_1,
  input  in_2,
  output [7:0] out_3
);

  memoria_um_bit memoria_um_bit_1 (.in_1(in_1[0]), .in_2(in_2), .out_3(out_3[0]));
  memoria_um_bit memoria_um_bit_2 (.in_1(in_1[1]), .in_2(in_2), .out_3(out_3[1]));
  memoria_um_bit memoria_um_bit_3 (.in_1(in_1[2]), .in_2(in_2), .out_3(out_3[2]));
  memoria_um_bit memoria_um_bit_4 (.in_1(in_1[3]), .in_2(in_2), .out_3(out_3[3]));
  memoria_um_bit memoria_um_bit_5 (.in_1(in_1[4]), .in_2(in_2), .out_3(out_3[4]));
  memoria_um_bit memoria_um_bit_6 (.in_1(in_1[5]), .in_2(in_2), .out_3(out_3[5]));
  memoria_um_bit memoria_um_bit_7 (.in_1(in_1[6]), .in_2(in_2), .out_3(out_3[6]));
  memoria_um_bit memoria_um_bit_8 (.in_1(in_1[7]), .in_2(in_2), .out_3(out_3[7]));
endmodule

module memoria_um_bit (
  input  in_1,
  input  in_2,
  output out_3
);

  wire nand_1_out, nand_2_out, nand_4_out;

  nand nand_1 (nand_1_out, in_1, in_2);
  nand nand_2 (nand_2_out, nand_1_out, in_2);
  nand nand_3 (out_3, nand_1_out, nand_4_out);
  nand nand_4 (nand_4_out, out_3, nand_2_out);
endmodule

module registrador_2bits (
  input  in_1,
  input  in_2,
  input  in_3,
  output out_4,
  output out_5
);

  memoria_um_bit memoria_um_bit_1 (.in_1(in_1), .in_2(in_3), .out_3(out_4));
  memoria_um_bit memoria_um_bit_2 (.in_1(in_2), .in_2(in_3), .out_3(out_5));
endmodule

module enable (
  input  [7:0] in_1,
  input  in_2,
  output [7:0] out_3
);

  wire [7:0] and_1_out;

  and and_1 (and_1_out[0], in_1[0], in_2);
  and and_2 (and_1_out[1], in_1[1], in_2);
  and and_3 (and_1_out[2], in_1[2], in_2);
  and and_4 (and_1_out[3], in_1[3], in_2);
  and and_5 (and_1_out[4], in_1[4], in_2);
  and and_6 (and_1_out[5], in_1[5], in_2);
  and and_7 (and_1_out[6], in_1[6], in_2);
  and and_8 (and_1_out[7], in_1[7], in_2);
  assign out_3 = in_2 ? and_1_out : 8'bz;  // Controlled_Buffer controlled_buffer_1
endmodule
