// Logisim project aula3.circ as structural Verilog: 15 circuits, main circuit main
module main (
  input  [7:0] input1,
  input  [7:0] in_2,
  input  [7:0] in_3,
  input  set,
  input  in_5,
  input  in_6,
  input  in_7,
  input  in_8,
  input  in_9,
  input  in_10,
  input  in_11,
  input  [7:0] in_12,
  input  write,
  input  eneable,
  output [7:0] out_15,
  output out_16,
  output out_17,
  output out_18,
  output out_19
);

  wire and_1_out, decoder_1_out0, decoder_1_out1, decoder_1_out2, decoder_1_out3, decoder_1_out4,
       decoder_1_out5, decoder_1_out6, decoder_1_out7, decoder_1_out8, decoder_1_out9, decoder_1_out10,
       decoder_1_out11, decoder_1_out12, decoder_1_out13, decoder_1_out14, decoder_1_out15, decoder_2_out0,
       decoder_2_out1, decoder_2_out2, decoder_2_out3, decoder_2_out4, decoder_2_out5, decoder_2_out6,
       decoder_2_out7, decoder_2_out8, decoder_2_out9, decoder_2_out10, decoder_2_out11, decoder_2_out12,
       decoder_2_out13, decoder_2_out14, decoder_2_out15;
  wire [7:0] memoria_8bits_1_out_3, memoria_8bits_2_out_3, memoria_8bits_3_out_3;

  deco_2x4 deco_2x4_1 (.in_1(in_10), .in_2(in_11), .out_3(out_16), .out_4(out_17), .out_5(out_18), .out_6(out_19));
  // Probe on out_15
  // Probe on memoria_8bits_1_out_3
  memoria_8bits memoria_8bits_1 (.in_1(input1), .in_2(set), .out_3(memoria_8bits_1_out_3));
  enable enable_1 (.in_1(memoria_8bits_1_out_3), .in_2(in_7), .out_3(out_15));
  Decoder #(.enable("false"), .select(4)) decoder_1 (
    .out0(decoder_1_out0), .out1(decoder_1_out1), .out2(decoder_1_out2), .out3(decoder_1_out3),
    .out4(decoder_1_out4), .out5(decoder_1_out5), .out6(decoder_1_out6), .out7(decoder_1_out7),
    .out8(decoder_1_out8), .out9(decoder_1_out9), .out10(decoder_1_out10), .out11(decoder_1_out11),
    .out12(decoder_1_out12), .out13(decoder_1_out13), .out14(decoder_1_out14), .out15(decoder_1_out15),
    .sel(in_12[7:4]));
  enable enable_2 (.in_1(memoria_8bits_2_out_3), .in_2(in_8), .out_3(out_15));
  // Probe on memoria_8bits_2_out_3
  memoria_8bits memoria_8bits_2 (.in_1(in_2), .in_2(in_5), .out_3(memoria_8bits_2_out_3));
  Decoder #(.enable("false"), .select(4)) decoder_2 (
    .out0(decoder_2_out0), .out1(decoder_2_out1), .out2(decoder_2_out2), .out3(decoder_2_out3),
    .out4(decoder_2_out4), .out5(decoder_2_out5), .out6(decoder_2_out6), .out7(decoder_2_out7),
    .out8(decoder_2_out8), .out9(decoder_2_out9), .out10(decoder_2_out10), .out11(decoder_2_out11),
    .out12(decoder_2_out12), .out13(decoder_2_out13), .out14(decoder_2_out14), .out15(decoder_2_out15),
    .sel(in_12[3:0]));
  enable enable_3 (.in_1(memoria_8bits_3_out_3), .in_2(in_9), .out_3(out_15));
  // Probe on memoria_8bits_3_out_3
  memoria_8bits memoria_8bits_3 (.in_1(in_3), .in_2(in_6), .out_3(memoria_8bits_3_out_3));
  and and_1 (and_1_out, decoder_1_out0, decoder_2_out0);
  // AND_Gate and_2 has open pins: in0=and_1_out, in1=write, out=open
  // AND_Gate and_3 has open pins: in0=and_1_out, in1=eneable, out=open

  // Other names for the same wires on the sheet: oe = eneable; we = write
endmodule

module memoria_8bits (
  input  [7:0] in_1,
  input  in_2,
  output [7:0] out_3
);

  memoria_um_bit memoria_um_bit_1 (.in_1(in_1[0]), .in_2(in_2), .out_3(out_3[0]));
  memoria_um_bit memoria_um_bit_2 (.in_1(in_1[1]), .in_2(in_2), .out_3(out_3[1]));
  memoria_um_bit memoria_um_bit_3 (.in_1(in_1[2]), .in_2(in_2), .out_3(out_3[2]));
  memoria_um_bit memoria_um_bit_4 (.in_1(in_1[3]), .in_2(in_2), .out_3(out_3[3]));
  memoria_um_bit memoria_um_bit_5 (.in_1(in_1[4]), .in_2(in_2), .out_3(out_3[4]));
  memoria_um_bit memoria_um_bit_6 (.in_1(in_1[5]), .in_2(in_2), .out_3(out_3[5]));
  memoria_um_bit memoria_um_bit_7 (.in_1(in_1[6]), .in_2(in_2), .out_3(out_3[6]));
  memoria_um_bit memoria_um_bit_8 (.in_1(in_1[7]), .in_2(in_2), .out_3(out_3[7]));
endmodule

module memoria_um_bit (
  input  in_1,
  input  in_2,
  output out_3
);

  wire nand_1_out, nand_2_out, nand_4_out;

  nand nand_1 (nand_1_out, in_1, in_2);
  nand nand_2 (nand_2_out, nand_1_out, in_2);
  nand nand_3 (out_3, nand_1_out, nand_4_out);
  nand nand_4 (nand_4_out, out_3, nand_2_out);
endmodule

module enable (
  input  [7:0] in_1,
  input  in_2,
  output [7:0] out_3
);

  wire [7:0] and_1_out;

  and and_1 (and_1_out[0], in_1[0], in_2);
  and and_2 (and_1_out[1], in_1[1], in_2);
  and and_3 (and_1_out[2], in_1[2], in_2);
  and and_4 (and_1_out[3], in_1[3], in_2);
  and and_5 (and_1_out[4], in_1[4], in_2);
  and and_6 (and_1_out[5], in_1[5], in_2);
  and and_7 (and_1_out[6], in_1[6], in_2);
  and and_8 (and_1_out[7], in_1[7], in_2);
  assign out_3 = in_2 ? and_1_out : 8'bz;  // Controlled_Buffer controlled_buffer_1
endmodule

module deco_2x4 (
  input  in_1,
  input  in_2,
  output out_3,
  output out_4,
  output out_5,
  output out_6
);

  wire not_1_out, not_2_out;

  not not_1 (not_1_out, in_1);
  not not_2 (not_2_out, in_2);
  and and_1 (out_3, not_1_out, not_2_out);
  and and_2 (out_4, not_2_out, in_1);
  and and_3 (out_5, not_1_out, in_2);
  and and_4 (out_6, in_1, in_2);
endmodule

module registrador (
  input  [7:0] in_1,
  input  in_2,
  input  in_3,
  output [7:0] out_4
);

  wire [7:0] memoria_um_bit_1_out_3;

  memoria_um_bit memoria_um_bit_1 (.in_1(in_1[0]), .in_2(in_2), .out_3(memoria_um_bit_1_out_3[0]));
  memoria_um_bit memoria_um_bit_2 (.in_1(in_1[1]), .in_2(in_2), .out_3(memoria_um_bit_1_out_3[1]));
  memoria_um_bit memoria_um_bit_3 (.in_1(in_1[2]), .in_2(in_2), .out_3(memoria_um_bit_1_out_3[2]));
  memoria_um_bit memoria_um_bit_4 (.in_1(in_1[3]), .in_2(in_2), .out_3(memoria_um_bit_1_out_3[3]));
  memoria_um_bit memoria_um_bit_5 (.in_1(in_1[4]), .in_2(in_2), .out_3(memoria_um_bit_1_out_3[4]));
  memoria_um_bit memoria_um_bit_6 (.in_1(in_1[5]), .in_2(in_2), .out_3(memoria_um_bit_1_out_3[5]));
  memoria_um_bit memoria_um_bit_7 (.in_1(in_1[6]), .in_2(in_2), .out_3(memoria_um_bit_1_out_3[6]));
  memoria_um_bit memoria_um_bit_8 (.in_1(in_1[7]), .in_2(in_2), .out_3(memoria_um_bit_1_out_3[7]));
  assign out_4 = in_3 ? memoria_um_bit_1_out_3 : 8'bz;  // Controlled_Buffer controlled_buffer_1
endmodule

module ramAula3 (
  input  in_1,
  input  in_2,
  input  in_3,
  input  in_4,
  input  [2:0] in_5,
  input  in_6,
  input  in_7,
  input  in_8,
  input  in_9,
  input  in_10,
  input  in_11,
  input  in_12,
  input  in_13,
  input  in_14,
  input  in_15,
  input  in_16,
  input  in_17,
  input  in_18,
  output carry_out,
  output A_larger_than_b,
  output A_equal_B,
  output zero
);

  wire or_1_out;
  wire [7:0] ACC_q, b1_saida, controlled_buffer_1_out, IAR_q, IR_q, mar_q, register_1_q, register_2_q,
       register_3_q, register_4_q, TMP_q, ula_1_out_5;

  ULA ula_1 (
    .A(controlled_buffer_1_out), .B(b1_saida), .out_5(ula_1_out_5), .in_1(in_5), .carry_out(carry_out),
    .A_larger_than_B(A_larger_than_b), .A_equal_B(A_equal_B), .zero(zero));
  Register TMP (.D(controlled_buffer_1_out), .Q(TMP_q), .clk(in_2));  // open: en, clr
  bus1 b1 (.entrada(TMP_q), .saida(b1_saida), .comando(in_3));
  Register ACC (.D(ula_1_out_5), .Q(ACC_q), .clk(in_17));  // open: en, clr
  assign controlled_buffer_1_out = in_18 ? ACC_q : 8'bz;  // Controlled_Buffer controlled_buffer_1
  Register register_1 (.D(controlled_buffer_1_out), .Q(register_1_q), .clk(in_7));  // open: en, clr
  assign controlled_buffer_1_out = in_11 ? register_1_q : 8'bz;  // Controlled_Buffer controlled_buffer_2
  Register register_2 (.D(controlled_buffer_1_out), .Q(register_2_q), .clk(in_8));  // open: en, clr
  assign controlled_buffer_1_out = in_12 ? register_2_q : 8'bz;  // Controlled_Buffer controlled_buffer_3
  Register IAR (.D(controlled_buffer_1_out), .Q(IAR_q));  // open: en, clk, clr
  assign controlled_buffer_1_out = in_15 ? IAR_q : 8'bz;  // Controlled_Buffer controlled_buffer_4
  assign controlled_buffer_1_out = in_13 ? register_3_q : 8'bz;  // Controlled_Buffer controlled_buffer_5
  Register register_3 (.D(controlled_buffer_1_out), .Q(register_3_q), .clk(in_9));  // open: en, clr
  Register IR (.D(controlled_buffer_1_out), .Q(IR_q));  // open: en, clk, clr
  assign controlled_buffer_1_out = in_14 ? register_4_q : 8'bz;  // Controlled_Buffer controlled_buffer_6
  Register register_4 (.D(controlled_buffer_1_out), .Q(register_4_q), .clk(in_10));  // open: en, clr
  assign controlled_buffer_1_out = in_16 ? IR_q : 8'bz;  // Controlled_Buffer controlled_buffer_7
  or or_1 (or_1_out, in_4, in_6);
  Register mar (.D(controlled_buffer_1_out), .Q(mar_q), .clk(in_1));  // open: en, clr
  RAM #(.databus("bidir")) ram_1 (.addr(mar_q), .we(in_4), .oe(in_6), .clk(or_1_out));  // open: data
endmodule

module shift_l (
  input  car_in,
  input  [7:0] in_2,
  output [7:0] out_3,
  output car_out
);


  assign car_out = in_2[7];
  assign out_3 = {in_2[6:0], car_in};
endmodule

module shift_r (
  input  [7:0] in_1,
  input  car_in,
  output [7:0] out_3,
  output car_out
);


  assign car_out = in_1[0];
  assign out_3 = {car_in, in_1[7:1]};
endmodule

module ULA (
  input  [2:0] in_1,
  input  [7:0] A,
  input  [7:0] B,
  output carry_out,
  output [7:0] out_5,
  output A_larger_than_B,
  output A_equal_B,
  output zero
);

  wire sl_car_out, somador_8bits_out_5, sr_car_out;
  wire [7:0] Porta_and_out, Porta_not_out, Porta_or_out, Porta_xor_out, sl_out_3, somador_8bits_out_4,
       sr_out_3;

  somador8 somador_8bits (.in_1(1'b0), .in_2(B), .in_3(A), .out_4(somador_8bits_out_4), .out_5(somador_8bits_out_5));
  shift_r sr (.in_1(A), .car_in(1'b0), .out_3(sr_out_3), .car_out(sr_car_out));
  shift_l sl (.car_in(1'b0), .in_2(A), .out_3(sl_out_3), .car_out(sl_car_out));
  assign Porta_not_out = ~A;  // NOT_Gate Porta_not, 8 bits wide
  assign Porta_and_out = B & A;  // AND_Gate Porta_and, 8 bits wide
  assign Porta_or_out = B | A;  // OR_Gate Porta_or, 8 bits wide
  assign Porta_xor_out = B ^ A;  // XOR_Gate Porta_xor, 8 bits wide
  Comparator comparator_1 (.a(A), .b(B), .gt(A_larger_than_B), .eq(A_equal_B));  // open: lt
  Multiplexer #(.select(3)) multiplexer_1 (
    .in0(somador_8bits_out_5), .in1(sr_car_out), .in2(sl_car_out), .in3(1'b0), .in4(1'b0), .in5(1'b0),
    .in6(1'b0), .in7(1'b0), .out(carry_out), .sel(in_1));
  Multiplexer #(.select(3), .width(8)) multiplexer_2 (
    .in0(somador_8bits_out_4), .in1(sr_out_3), .in2(sl_out_3), .in3(Porta_not_out), .in4(Porta_and_out),
    .in5(Porta_or_out), .in6(Porta_xor_out), .in7(A), .out(out_5), .sel(in_1));
  nor nor_1 (zero, out_5[0], out_5[1], out_5[2], out_5[3], out_5[4], out_5[5], out_5[6], out_5[7]);
endmodule

module somador1 (
  input  in_1,
  input  in_2,
  input  in_3,
  output out_4,
  output out_5
);

  wire and_1_out, and_2_out, and_3_out, xor_1_out;

  xor xor_1 (xor_1_out, in_1, in_2);
  and and_1 (and_1_out, in_2, in_3);
  and and_2 (and_2_out, in_2, in_1);
  and and_3 (and_3_out, in_3, in_1);
  xor xor_2 (out_4, xor_1_out, in_3);
  or or_1 (out_5, and_1_out, and_2_out, and_3_out);
endmodule

module somador8 (
  input  in_1,
  input  [7:0] in_2,
  input  [7:0] in_3,
  output [7:0] out_4,
  output out_5
);

  wire somador1_1_out_5, somador1_2_out_5, somador1_3_out_5, somador1_4_out_5, somador1_5_out_5,
       somador1_6_out_5, somador1_7_out_5;

  somador1 somador1_1 (.in_2(in_2[0]), .in_3(in_3[0]), .in_1(in_1), .out_4(out_4[0]), .out_5(somador1_1_out_5));
  somador1 somador1_2 (
    .in_2(in_2[1]), .in_3(in_3[1]), .in_1(somador1_1_out_5), .out_4(out_4[1]), .out_5(somador1_2_out_5));
  somador1 somador1_3 (
    .in_2(in_2[2]), .in_3(in_3[2]), .in_1(somador1_2_out_5), .out_4(out_4[2]), .out_5(somador1_3_out_5));
  somador1 somador1_4 (
    .in_2(in_2[3]), .in_3(in_3[3]), .in_1(somador1_3_out_5), .out_4(out_4[3]), .out_5(somador1_4_out_5));
  somador1 somador1_5 (
    .in_2(in_2[4]), .in_3(in_3[4]), .in_1(somador1_4_out_5), .out_4(out_4[4]), .out_5(somador1_5_out_5));
  somador1 somador1_6 (
    .in_2(in_2[5]), .in_3(in_3[5]), .in_1(somador1_5_out_5), .out_4(out_4[5]), .out_5(somador1_6_out_5));
  somador1 somador1_7 (
    .in_2(in_2[6]), .in_3(in_3[6]), .in_1(somador1_6_out_5), .out_4(out_4[6]), .out_5(somador1_7_out_5));
  somador1 somador1_8 (.in_2(in_2[7]), .in_3(in_3[7]), .in_1(somador1_7_out_5), .out_4(out_4[7]), .out_5(out_5));
endmodule

module clk (
  output setclock,
  output enableclock
);

  wire clock_1_out, not_1_out, t_ff_1_q;

  Clock clock_1 (.out(clock_1_out));
  not not_1 (not_1_out, clock_1_out);
  T_Flip_Flop t_ff_1 (.clk(clock_1_out), .T(1'b1), .Q(t_ff_1_q));  // open: Qn, preset, reset
  and and_1 (setclock, not_1_out, t_ff_1_q);
  or or_1 (enableclock, t_ff_1_q, clock_1_out);
endmodule

module uc (
  output init,
  output s1,
  output s2,
  output s3,
  output s4,
  output s5,
  output s6
);

  wire clk_1_enableclock, decoder_1_out7;
  wire [2:0] counter_1_q;

  clk clk_1 (.enableclock(clk_1_enableclock));  // open: setclock
  Counter #(.max('h7), .width(3)) counter_1 (
    .D(3'b001), .Q(counter_1_q), .clk(clk_1_enableclock), .clr(decoder_1_out7));  // open: load, count, carry, up
  Decoder #(.enable("false"), .select(3)) decoder_1 (
    .out0(init), .out1(s1), .out2(s2), .out3(s3), .out4(s4), .out5(s5), .out6(s6), .out7(decoder_1_out7),
    .sel(counter_1_q));
endmodule

module bus1 (
  input  [7:0] entrada,
  input  comando,
  output [7:0] saida
);

  Multiplexer #(.width(8)) multiplexer_1 (.in0(entrada), .in1(8'h1), .out(saida), .sel(comando));
endmodule
