// Logisim project projeto-OC_16bits.circ as structural Verilog: 20 circuits, main circuit main
module main (
  input  in_1
);

  wire and_1_out, comparator_1_eq, data, flags_1_a_larger, flags_1_carry_out, flags_1_equal, flags_1_zero,
       i_o, input_ena, input_set, monitor_1_out_6, monitor_1_out_7, or_1_out, register_1_q, teclado_1_out_8,
       teclado_1_out_9, uc_1_acc_ena, uc_1_acc_set, uc_1_bus1_ena, uc_1_flags_set, uc_1_iar_ena,
       uc_1_iar_set, uc_1_init, uc_1_ir_set, uc_1_mar_set, uc_1_r0_e, uc_1_r0_s, uc_1_r1_e, uc_1_r1_s,
       uc_1_r2_e, uc_1_r2_s, uc_1_r3_e, uc_1_r3_s, uc_1_ram_ena, uc_1_ram_set, uc_1_tmp_set, ula_1_a_equal_b,
       ula_1_a_larger_than_b, ula_1_carry_out, ula_1_zero;
  wire [2:0] uc_1_to_ula;
  wire [6:0] keyboard_1_data, monitor_1_out_5;
  wire [15:0] ACC_q, b1_saida, controlled_buffer_1_out, controlled_buffer_7_out, IAR_q, IR_q, mar_q, R0_q,
       R1_q, R2_q, R3_q, TMP_q, ula_1_out_5;

  // Probe on TMP_q
  // Probe on b1_saida
  // Probe on ula_1_out_5
  bus1 b1 (.entrada(TMP_q), .saida(b1_saida), .comando(uc_1_bus1_ena));
  ULA ula_1 (
    .A(controlled_buffer_1_out), .B(b1_saida), .out_5(ula_1_out_5), .in_1(uc_1_to_ula),
    .carry_out(ula_1_carry_out), .A_larger_than_B(ula_1_a_larger_than_b), .A_equal_B(ula_1_a_equal_b),
    .zero(ula_1_zero));
  Register #(.width(16)) TMP (.D(controlled_buffer_1_out), .Q(TMP_q), .clk(uc_1_tmp_set));  // open: en, clr
  Flags flags_1 (
    .c_in(ula_1_carry_out), .a_in(ula_1_a_larger_than_b), .e_in(ula_1_a_equal_b), .z_in(ula_1_zero),
    .carry_out(flags_1_carry_out), .a_larger(flags_1_a_larger), .equal(flags_1_equal), .zero(flags_1_zero),
    .set_flags(uc_1_flags_set));
  Register #(.width(16)) ACC (.D(ula_1_out_5), .Q(ACC_q), .clk(uc_1_acc_set));  // open: en, clr
  assign controlled_buffer_1_out = uc_1_acc_ena ? ACC_q : 16'bz;  // Controlled_Buffer controlled_buffer_1
  teclado teclado_1 (
    .input_ena(input_ena), .input_set(input_set), .data(data), .i_o(i_o), .in_1(controlled_buffer_1_out),
    .out_7(controlled_buffer_1_out), .in_3(keyboard_1_data), .out_8(teclado_1_out_8), .out_9(teclado_1_out_9));
  assign controlled_buffer_1_out = uc_1_r3_e ? R3_q : 16'bz;  // Controlled_Buffer controlled_buffer_2
  Register #(.width(16)) R3 (.D(controlled_buffer_1_out), .Q(R3_q), .clk(uc_1_r3_s));  // open: en, clr
  Register #(.width(16)) IR (.D(controlled_buffer_1_out), .Q(IR_q), .clk(uc_1_ir_set));  // open: en, clr
  Keyboard keyboard_1 (.clk(teclado_1_out_8), .re(teclado_1_out_9), .clr(in_1), .data(keyboard_1_data));  // open: avail
  assign controlled_buffer_1_out = uc_1_r2_e ? R2_q : 16'bz;  // Controlled_Buffer controlled_buffer_3
  Register #(.width(16)) R2 (.D(controlled_buffer_1_out), .Q(R2_q), .clk(uc_1_r2_s));  // open: en, clr
  assign controlled_buffer_1_out = uc_1_r1_e ? R1_q : 16'bz;  // Controlled_Buffer controlled_buffer_4
  Register #(.width(16)) R1 (.D(controlled_buffer_1_out), .Q(R1_q), .clk(uc_1_r1_s));  // open: en, clr
  Register #(.width(16)) IAR (.D(controlled_buffer_1_out), .Q(IAR_q), .clk(uc_1_iar_set));  // open: en, clr
  assign controlled_buffer_1_out = uc_1_iar_ena ? IAR_q : 16'bz;  // Controlled_Buffer controlled_buffer_5
  assign controlled_buffer_1_out = uc_1_r0_e ? R0_q : 16'bz;  // Controlled_Buffer controlled_buffer_6
  Register #(.width(16)) R0 (.D(controlled_buffer_1_out), .Q(R0_q), .clk(uc_1_r0_s));  // open: en, clr
  LED led_1 (.in(uc_1_init));
  uc uc_1 (
    .Carry_out(flags_1_carry_out), .A_larger(flags_1_a_larger), .Equal(flags_1_equal), .zero(flags_1_zero),
    .IR(IR_q), .R0_E(uc_1_r0_e), .R1_E(uc_1_r1_e), .R2_E(uc_1_r2_e), .R3_E(uc_1_r3_e), .Data_Address(data),
    .in_out_put(i_o), .init(uc_1_init), .I_O_clk_s(input_set), .RAM_SET(uc_1_ram_set),
    .TMP_SET(uc_1_tmp_set), .Flags_SET(uc_1_flags_set), .IR_SET(uc_1_ir_set), .MAR_SET(uc_1_mar_set),
    .IAR_SET(uc_1_iar_set), .ACC_SET(uc_1_acc_set), .R0_S(uc_1_r0_s), .R1_S(uc_1_r1_s), .R2_S(uc_1_r2_s),
    .R3_S(uc_1_r3_s), .IAR_ena(uc_1_iar_ena), .ACC_ena(uc_1_acc_ena), .I_O_clk_ena(input_ena),
    .Bus1_ena(uc_1_bus1_ena), .RAM_ena(uc_1_ram_ena), .to_ula(uc_1_to_ula));
  monitor monitor_1 (
    .input_set(input_set), .data(data), .i_o(i_o), .in_1(controlled_buffer_1_out), .out_5(monitor_1_out_5),
    .out_6(monitor_1_out_6), .out_7(monitor_1_out_7));
  Register #(.width(16)) mar (.D(controlled_buffer_1_out), .Q(mar_q), .clk(uc_1_mar_set));  // open: en, clr
  TTY tty_1 (.data(monitor_1_out_5), .clk(monitor_1_out_6), .we(monitor_1_out_7));  // open: clr
  or or_1 (or_1_out, uc_1_ram_set, uc_1_ram_ena);
  RAM #(.addrWidth(16), .dataWidth(16), .databus("bidir"), .\type ("nonvolatile")) ram_1 (
    .addr(mar_q), .we(uc_1_ram_set), .oe(uc_1_ram_ena), .clk(or_1_out));  // open: data
  and and_1 (and_1_out, input_set, data, i_o);
  Comparator #(.width(16)) comparator_1 (.a(controlled_buffer_1_out), .b(16'h2), .eq(comparator_1_eq));  // open: gt, lt
  Register #(.width(1)) register_1 (.D(comparator_1_eq), .Q(register_1_q), .clk(and_1_out));  // open: en, clr
  // Probe on controlled_buffer_1_out
  assign controlled_buffer_7_out = input_set ? controlled_buffer_1_out : 16'bz;  // Controlled_Buffer controlled_buffer_7
  // PortIO #(.number(16)) portio_1: pin names not known; wires that end beside it: register_1_q, controlled_buffer_7_out

  // Notes on the sheet:
  //   Michael Willian Pereira Vieira - 22400829
endmodule

module memoria_8bits (
  input  [7:0] in_1,
  input  in_2,
  output [7:0] out_3
);

  memoria_um_bit memoria_um_bit_1 (.in_1(in_1[0]), .in_2(in_2), .out_3(out_3[0]));
  memoria_um_bit memoria_um_bit_2 (.in_1(in_1[1]), .in_2(in_2), .out_3(out_3[1]));
  memoria_um_bit memoria_um_bit_3 (.in_1(in_1[2]), .in_2(in_2), .out_3(out_3[2]));
  memoria_um_bit memoria_um_bit_4 (.in_1(in_1[3]), .in_2(in_2), .out_3(out_3[3]));
  memoria_um_bit memoria_um_bit_5 (.in_1(in_1[4]), .in_2(in_2), .out_3(out_3[4]));
  memoria_um_bit memoria_um_bit_6 (.in_1(in_1[5]), .in_2(in_2), .out_3(out_3[5]));
  memoria_um_bit memoria_um_bit_7 (.in_1(in_1[6]), .in_2(in_2), .out_3(out_3[6]));
  memoria_um_bit memoria_um_bit_8 (.in_1(in_1[7]), .in_2(in_2), .out_3(out_3[7]));
endmodule

module memoria_um_bit (
  input  in_1,
  input  in_2,
  output out_3
);

  wire nand_1_out, nand_2_out, nand_4_out;

  nand nand_1 (nand_1_out, in_1, in_2);
  nand nand_2 (nand_2_out, nand_1_out, in_2);
  nand nand_3 (out_3, nand_1_out, nand_4_out);
  nand nand_4 (nand_4_out, out_3, nand_2_out);
endmodule

module enable (
  input  [7:0] in_1,
  input  in_2,
  output [7:0] out_3
);

  wire [7:0] and_1_out;

  and and_1 (and_1_out[0], in_1[0], in_2);
  and and_2 (and_1_out[1], in_1[1], in_2);
  and and_3 (and_1_out[2], in_1[2], in_2);
  and and_4 (and_1_out[3], in_1[3], in_2);
  and and_5 (and_1_out[4], in_1[4], in_2);
  and and_6 (and_1_out[5], in_1[5], in_2);
  and and_7 (and_1_out[6], in_1[6], in_2);
  and and_8 (and_1_out[7], in_1[7], in_2);
  assign out_3 = in_2 ? and_1_out : 8'bz;  // Controlled_Buffer controlled_buffer_1
endmodule

module deco_2x4 (
  input  in_1,
  input  in_2,
  output out_3,
  output out_4,
  output out_5,
  output out_6
);

  wire not_1_out, not_2_out;

  not not_1 (not_1_out, in_1);
  not not_2 (not_2_out, in_2);
  and and_1 (out_3, not_1_out, not_2_out);
  and and_2 (out_4, not_2_out, in_1);
  and and_3 (out_5, not_1_out, in_2);
  and and_4 (out_6, in_1, in_2);
endmodule

module registrador (
  input  [7:0] in_1,
  input  in_2,
  input  in_3,
  output [7:0] out_4
);

  wire [7:0] memoria_um_bit_1_out_3;

  memoria_um_bit memoria_um_bit_1 (.in_1(in_1[0]), .in_2(in_2), .out_3(memoria_um_bit_1_out_3[0]));
  memoria_um_bit memoria_um_bit_2 (.in_1(in_1[1]), .in_2(in_2), .out_3(memoria_um_bit_1_out_3[1]));
  memoria_um_bit memoria_um_bit_3 (.in_1(in_1[2]), .in_2(in_2), .out_3(memoria_um_bit_1_out_3[2]));
  memoria_um_bit memoria_um_bit_4 (.in_1(in_1[3]), .in_2(in_2), .out_3(memoria_um_bit_1_out_3[3]));
  memoria_um_bit memoria_um_bit_5 (.in_1(in_1[4]), .in_2(in_2), .out_3(memoria_um_bit_1_out_3[4]));
  memoria_um_bit memoria_um_bit_6 (.in_1(in_1[5]), .in_2(in_2), .out_3(memoria_um_bit_1_out_3[5]));
  memoria_um_bit memoria_um_bit_7 (.in_1(in_1[6]), .in_2(in_2), .out_3(memoria_um_bit_1_out_3[6]));
  memoria_um_bit memoria_um_bit_8 (.in_1(in_1[7]), .in_2(in_2), .out_3(memoria_um_bit_1_out_3[7]));
  assign out_4 = in_3 ? memoria_um_bit_1_out_3 : 8'bz;  // Controlled_Buffer controlled_buffer_1
endmodule

module ramAula3 (
);

  wire flags_1_a_larger, flags_1_carry_out, flags_1_equal, flags_1_zero, or_1_out, uc_1_acc_ena,
       uc_1_acc_set, uc_1_bus1_ena, uc_1_flags_set, uc_1_iar_ena, uc_1_iar_set, uc_1_init, uc_1_ir_set,
       uc_1_mar_set, uc_1_r0_e, uc_1_r0_s, uc_1_r1_e, uc_1_r1_s, uc_1_r2_e, uc_1_r2_s, uc_1_r3_e, uc_1_r3_s,
       uc_1_ram_ena, uc_1_ram_set, uc_1_tmp_set, ula_1_p5, ula_1_p6, ula_1_p7, ula_1_p8;
  wire [2:0] ula_1_p4;
  wire [7:0] ACC_q, IAR_q, mar_q, R0_q, R1_q, R2_q, R3_q, ula_1_p1, ula_1_p2;
  wire [15:0] IR_q, TMP_q, ula_1_p3;

  // ULA ula_1: pin names not known; wires that end beside it: ula_1_p1, ula_1_p2, ula_1_p3, ula_1_p4, ula_1_p5, ula_1_p6, ula_1_p7, ula_1_p8
  Register TMP (.D(ula_1_p1), .Q(TMP_q[7:0]), .clk(uc_1_tmp_set));  // open: en, clr
  bus1 b1 (.entrada(TMP_q), .saida(ula_1_p3), .comando(uc_1_bus1_ena));
  Flags flags_1 (
    .c_in(ula_1_p5), .a_in(ula_1_p6), .e_in(ula_1_p7), .z_in(ula_1_p8), .carry_out(flags_1_carry_out),
    .a_larger(flags_1_a_larger), .equal(flags_1_equal), .zero(flags_1_zero), .set_flags(uc_1_flags_set));
  Register ACC (.D(ula_1_p2), .Q(ACC_q), .clk(uc_1_acc_set));  // open: en, clr
  assign ula_1_p1 = uc_1_acc_ena ? ACC_q : 8'bz;  // Controlled_Buffer controlled_buffer_1
  assign ula_1_p1 = uc_1_r3_e ? R3_q : 8'bz;  // Controlled_Buffer controlled_buffer_2
  Register R3 (.D(ula_1_p1), .Q(R3_q), .clk(uc_1_r3_s));  // open: en, clr
  Register IR (.D(ula_1_p1), .Q(IR_q[7:0]), .clk(uc_1_ir_set));  // open: en, clr
  assign ula_1_p1 = uc_1_r2_e ? R2_q : 8'bz;  // Controlled_Buffer controlled_buffer_3
  Register R2 (.D(ula_1_p1), .Q(R2_q), .clk(uc_1_r2_s));  // open: en, clr
  Register R1 (.D(ula_1_p1), .Q(R1_q), .clk(uc_1_r1_s));  // open: en, clr
  Register IAR (.D(ula_1_p1), .Q(IAR_q), .clk(uc_1_iar_set));  // open: en, clr
  assign ula_1_p1 = uc_1_r1_e ? R1_q : 8'bz;  // Controlled_Buffer controlled_buffer_4
  assign ula_1_p1 = uc_1_iar_ena ? IAR_q : 8'bz;  // Controlled_Buffer controlled_buffer_5
  assign ula_1_p1 = uc_1_r0_e ? R0_q : 8'bz;  // Controlled_Buffer controlled_buffer_6
  Register R0 (.D(ula_1_p1), .Q(R0_q), .clk(uc_1_r0_s));  // open: en, clr
  LED led_1 (.in(uc_1_init));
  uc uc_1 (
    .Carry_out(flags_1_carry_out), .A_larger(flags_1_a_larger), .Equal(flags_1_equal), .zero(flags_1_zero),
    .IR(IR_q), .R0_E(uc_1_r0_e), .R1_E(uc_1_r1_e), .R2_E(uc_1_r2_e), .R3_E(uc_1_r3_e), .init(uc_1_init),
    .RAM_SET(uc_1_ram_set), .TMP_SET(uc_1_tmp_set), .Flags_SET(uc_1_flags_set), .IR_SET(uc_1_ir_set),
    .MAR_SET(uc_1_mar_set), .IAR_SET(uc_1_iar_set), .ACC_SET(uc_1_acc_set), .R0_S(uc_1_r0_s),
    .R1_S(uc_1_r1_s), .R2_S(uc_1_r2_s), .R3_S(uc_1_r3_s), .IAR_ena(uc_1_iar_ena), .ACC_ena(uc_1_acc_ena),
    .Bus1_ena(uc_1_bus1_ena), .RAM_ena(uc_1_ram_ena), .to_ula(ula_1_p4));  // open: Data_Address, in_out_put, I_O_clk_s, I_O_clk_ena
  Register mar (.D(ula_1_p1), .Q(mar_q), .clk(uc_1_mar_set));  // open: en, clr
  RAM #(.databus("bidir")) ram_1 (.addr(mar_q), .we(uc_1_ram_set), .oe(uc_1_ram_ena), .clk(or_1_out));  // open: data
  or or_1 (or_1_out, uc_1_ram_set, uc_1_ram_ena);
  // Pins of 8 and 16 bits meet at TMP_q
  // Pins of 8 and 16 bits meet at IR_q
endmodule

module shift_l (
  input  car_in,
  input  [15:0] in_2,
  output [15:0] out_3,
  output car_out
);


  assign car_out = in_2[15];
  assign out_3 = {in_2[14:0], car_in};
endmodule

module shift_r (
  input  [15:0] in_1,
  input  car_in,
  output [15:0] out_3,
  output car_out
);


  assign car_out = in_1[0];
  assign out_3 = {car_in, in_1[15:1]};
endmodule

module ULA (
  input  [2:0] in_1,
  input  [15:0] A,
  input  [15:0] B,
  output carry_out,
  output [15:0] out_5,
  output A_larger_than_B,
  output A_equal_B,
  output zero
);

  wire sl_car_out, somador_16bits_out_5, sr_car_out;
  wire [15:0] not_1_out, Porta_and_out, Porta_or_out, Porta_xor_out, sl_out_3, somador_16bits_out_4, sr_out_3;

  somador8 somador_16bits (.in_1(1'b0), .in_2(B), .in_3(A), .out_4(somador_16bits_out_4), .out_5(somador_16bits_out_5));
  shift_r sr (.in_1(A), .car_in(1'b0), .out_3(sr_out_3), .car_out(sr_car_out));
  shift_l sl (.car_in(1'b0), .in_2(A), .out_3(sl_out_3), .car_out(sl_car_out));
  assign not_1_out = ~A;  // NOT_Gate not_1, 16 bits wide
  assign Porta_and_out = B & A;  // AND_Gate Porta_and, 16 bits wide
  assign Porta_or_out = B | A;  // OR_Gate Porta_or, 16 bits wide
  assign Porta_xor_out = B ^ A;  // XOR_Gate Porta_xor, 16 bits wide
  Comparator #(.width(16)) comparator_1 (.a(A), .b(B), .gt(A_larger_than_B), .eq(A_equal_B));  // open: lt
  // Probe on somador_16bits_out_4
  Multiplexer #(.select(3)) multiplexer_1 (
    .in0(somador_16bits_out_5), .in1(sr_car_out), .in2(sl_car_out), .in3(1'b0), .in4(1'b0), .in5(1'b0),
    .in6(1'b0), .in7(1'b0), .out(carry_out), .sel(in_1));
  Multiplexer #(.select(3), .width(16)) multiplexer_2 (
    .in0(somador_16bits_out_4), .in1(sr_out_3), .in2(sl_out_3), .in3(not_1_out), .in4(Porta_and_out),
    .in5(Porta_or_out), .in6(Porta_xor_out), .in7(A), .out(out_5), .sel(in_1));
  nor nor_1 (zero, out_5[0], out_5[1], out_5[2], out_5[3], out_5[4], out_5[5], out_5[6], out_5[7], out_5[8], out_5[9], out_5[10], out_5[11], out_5[12], out_5[13], out_5[14], out_5[15]);
endmodule

module somador1 (
  input  in_1,
  input  in_2,
  input  in_3,
  output out_4,
  output out_5
);

  wire and_1_out, and_2_out, and_3_out, xor_1_out;

  xor xor_1 (xor_1_out, in_1, in_2);
  and and_1 (and_1_out, in_2, in_3);
  and and_2 (and_2_out, in_2, in_1);
  and and_3 (and_3_out, in_3, in_1);
  xor xor_2 (out_4, xor_1_out, in_3);
  or or_1 (out_5, and_1_out, and_2_out, and_3_out);
endmodule

module somador8 (
  input  in_1,
  input  [15:0] in_2,
  input  [15:0] in_3,
  output [15:0] out_4,
  output out_5
);

  wire somador1_1_out_5, somador1_2_out_5, somador1_3_out_5, somador1_4_out_5, somador1_5_out_5,
       somador1_6_out_5, somador1_7_out_5, somador1_8_out_5, somador1_9_out_5, somador1_10_out_5,
       somador1_11_out_5, somador1_12_out_5, somador1_13_out_5, somador1_14_out_5, somador1_15_out_5;

  somador1 somador1_1 (.in_2(in_2[0]), .in_3(in_3[0]), .in_1(in_1), .out_4(out_4[0]), .out_5(somador1_1_out_5));
  somador1 somador1_2 (
    .in_2(in_2[1]), .in_3(in_3[1]), .in_1(somador1_1_out_5), .out_4(out_4[1]), .out_5(somador1_2_out_5));
  somador1 somador1_3 (
    .in_2(in_2[2]), .in_3(in_3[2]), .in_1(somador1_2_out_5), .out_4(out_4[2]), .out_5(somador1_3_out_5));
  somador1 somador1_4 (
    .in_2(in_2[3]), .in_3(in_3[3]), .in_1(somador1_3_out_5), .out_4(out_4[3]), .out_5(somador1_4_out_5));
  somador1 somador1_5 (
    .in_2(in_2[4]), .in_3(in_3[4]), .in_1(somador1_4_out_5), .out_4(out_4[4]), .out_5(somador1_5_out_5));
  somador1 somador1_6 (
    .in_2(in_2[5]), .in_3(in_3[5]), .in_1(somador1_5_out_5), .out_4(out_4[5]), .out_5(somador1_6_out_5));
  somador1 somador1_7 (
    .in_2(in_2[6]), .in_3(in_3[6]), .in_1(somador1_6_out_5), .out_4(out_4[6]), .out_5(somador1_7_out_5));
  somador1 somador1_8 (
    .in_2(in_2[7]), .in_3(in_3[7]), .in_1(somador1_7_out_5), .out_4(out_4[7]), .out_5(somador1_8_out_5));
  somador1 somador1_9 (
    .in_2(in_2[8]), .in_3(in_3[8]), .in_1(somador1_8_out_5), .out_4(out_4[8]), .out_5(somador1_9_out_5));
  somador1 somador1_10 (
    .in_2(in_2[9]), .in_3(in_3[9]), .in_1(somador1_9_out_5), .out_4(out_4[9]), .out_5(somador1_10_out_5));
  somador1 somador1_11 (
    .in_2(in_2[10]), .in_3(in_3[10]), .in_1(somador1_10_out_5), .out_4(out_4[10]), .out_5(somador1_11_out_5));
  somador1 somador1_12 (
    .in_2(in_2[11]), .in_3(in_3[11]), .in_1(somador1_11_out_5), .out_4(out_4[11]), .out_5(somador1_12_out_5));
  somador1 somador1_13 (
    .in_2(in_2[12]), .in_3(in_3[12]), .in_1(somador1_12_out_5), .out_4(out_4[12]), .out_5(somador1_13_out_5));
  somador1 somador1_14 (
    .in_2(in_2[13]), .in_3(in_3[13]), .in_1(somador1_13_out_5), .out_4(out_4[13]), .out_5(somador1_14_out_5));
  somador1 somador1_15 (
    .in_2(in_2[14]), .in_3(in_3[14]), .in_1(somador1_14_out_5), .out_4(out_4[14]), .out_5(somador1_15_out_5));
  somador1 somador1_16 (.in_2(in_2[15]), .in_3(in_3[15]), .in_1(somador1_15_out_5), .out_4(out_4[15]), .out_5(out_5));
endmodule

module clk (
  output setclock,
  output enableclock
);

  wire clock_1_out, not_1_out, t_ff_1_q;

  Clock clock_1 (.out(clock_1_out));
  not not_1 (not_1_out, clock_1_out);
  T_Flip_Flop t_ff_1 (.clk(clock_1_out), .T(1'b1), .Q(t_ff_1_q));  // open: Qn, preset, reset
  and and_1 (setclock, not_1_out, t_ff_1_q);
  or or_1 (enableclock, t_ff_1_q, clock_1_out);
endmodule

module uc (
  input  Carry_out,
  input  A_larger,
  input  Equal,
  input  zero,
  input  [15:0] IR,
  output init,
  output IR_SET,
  output Bus1_ena,
  output MAR_SET,
  output IAR_ena,
  output IAR_SET,
  output RAM_ena,
  output ACC_SET,
  output RAM_SET,
  output ACC_ena,
  output TMP_SET,
  output I_O_clk_ena,
  output Flags_SET,
  output I_O_clk_s,
  output R0_E,
  output R0_S,
  output R1_S,
  output R1_E,
  output R2_S,
  output R3_S,
  output R2_E,
  output R3_E,
  output Data_Address,
  output in_out_put,
  output [2:0] to_ula
);

  wire A_out, acc_en_out, acc_s_out, and_5_out, and_6_out, and_7_out, and_8_out, and_9_out, and_10_out,
       and_11_out, and_12_out, and_16_out, and_17_out, and_18_out, and_19_out, and_20_out, and_21_out,
       and_22_out, and_23_out, and_24_out, and_25_out, and_26_out, and_27_out, and_28_out, and_29_out,
       and_30_out, and_31_out, and_32_out, and_33_out, and_34_out, and_35_out, and_36_out, and_37_out,
       and_38_out, and_39_out, and_40_out, and_41_out, and_42_out, and_43_out, C_out, clk_1_enableclock,
       clk_1_setclock, decoder_1_out0, decoder_1_out1, decoder_1_out2, decoder_1_out3, decoder_2_out0,
       decoder_2_out1, decoder_2_out2, decoder_2_out3, decoder_3_out0, decoder_3_out1, decoder_3_out2,
       decoder_3_out3, decoder_3_out4, decoder_3_out5, decoder_3_out6, decoder_3_out7, decoder_4_out0,
       decoder_4_out1, decoder_4_out2, decoder_4_out3, E_out, flags_s_out, iar_en_out, iar_s_out, mar_s_out,
       not_1_out, not_2_out, not_3_out, or_5_out, ram_en_out, reg_A_en_out, reg_B_en_out, reg_B_s_out,
       stepper_1_s1, stepper_1_s2, stepper_1_s3, stepper_1_s4, stepper_1_s5, stepper_1_s6, Z_out;

  or or_1 (R0_E, and_5_out, and_9_out);
  or or_2 (R1_E, and_6_out, and_10_out);
  or or_3 (R2_E, and_7_out, and_11_out);
  or or_4 (R3_E, and_8_out, and_12_out);
  clk clk_1 (.setclock(clk_1_setclock), .enableclock(clk_1_enableclock));
  and and_1 (IAR_ena, clk_1_enableclock, iar_en_out);
  and and_2 (RAM_ena, clk_1_enableclock, ram_en_out);
  and and_3 (ACC_ena, clk_1_enableclock, acc_en_out);
  and and_4 (I_O_clk_ena, clk_1_enableclock, and_40_out);
  and and_5 (and_5_out, clk_1_enableclock, reg_B_en_out, decoder_1_out0);
  and and_6 (and_6_out, clk_1_enableclock, reg_B_en_out, decoder_1_out1);
  and and_7 (and_7_out, clk_1_enableclock, reg_B_en_out, decoder_1_out2);
  and and_8 (and_8_out, clk_1_enableclock, reg_B_en_out, decoder_1_out3);
  and and_9 (and_9_out, clk_1_enableclock, reg_A_en_out, decoder_2_out0);
  and and_10 (and_10_out, clk_1_enableclock, reg_A_en_out, decoder_2_out1);
  and and_11 (and_11_out, clk_1_enableclock, reg_A_en_out, decoder_2_out2);
  and and_12 (and_12_out, clk_1_enableclock, reg_A_en_out, decoder_2_out3);
  Decoder #(.enable("false"), .select(2)) decoder_1 (
    .out0(decoder_1_out0), .out1(decoder_1_out1), .out2(decoder_1_out2), .out3(decoder_1_out3), .sel(IR[1:0]));
  Decoder #(.enable("false"), .select(2)) decoder_2 (
    .out0(decoder_2_out0), .out1(decoder_2_out1), .out2(decoder_2_out2), .out3(decoder_2_out3), .sel(IR[3:2]));
  and and_13 (to_ula[0], stepper_1_s5, IR[15], IR[12]);
  and and_14 (to_ula[1], stepper_1_s5, IR[15], IR[13]);
  and and_15 (to_ula[2], stepper_1_s5, IR[15], IR[14]);
  or bus1_en (Bus1_ena, stepper_1_s1, and_31_out, and_30_out, and_27_out);
  or iar_en (iar_en_out, stepper_1_s1, and_27_out, and_29_out, and_30_out);
  or ram_en (ram_en_out, stepper_1_s2, and_43_out, and_38_out, and_37_out, and_35_out);
  or acc_en (acc_en_out, stepper_1_s3, and_39_out, and_42_out, and_41_out);
  or reg_B_en (reg_B_en_out, and_24_out, and_36_out, and_28_out, and_32_out);
  or reg_A_en (reg_A_en_out, and_26_out, and_25_out, and_34_out);
  not not_1 (not_1_out, IR[15]);
  Decoder #(.enable("false"), .select(3)) decoder_3 (
    .out0(decoder_3_out0), .out1(decoder_3_out1), .out2(decoder_3_out2), .out3(decoder_3_out3),
    .out4(decoder_3_out4), .out5(decoder_3_out5), .out6(decoder_3_out6), .out7(decoder_3_out7),
    .sel(IR[14:12]));
  and and_16 (and_16_out, not_1_out, decoder_3_out0);
  and and_17 (and_17_out, not_1_out, decoder_3_out1);
  and and_18 (and_18_out, not_1_out, decoder_3_out2);
  and and_19 (and_19_out, not_1_out, decoder_3_out3);
  and and_20 (and_20_out, not_1_out, decoder_3_out4);
  and and_21 (and_21_out, not_1_out, decoder_3_out5);
  and and_22 (and_22_out, not_1_out, decoder_3_out6);
  and and_23 (and_23_out, not_1_out, decoder_3_out7);
  and and_24 (and_24_out, stepper_1_s4, IR[15]);
  and and_25 (and_25_out, stepper_1_s4, and_16_out);
  and and_26 (and_26_out, stepper_1_s4, and_17_out);
  and and_27 (and_27_out, stepper_1_s4, and_18_out);
  and and_28 (and_28_out, stepper_1_s4, and_19_out);
  and and_29 (and_29_out, stepper_1_s4, and_20_out);
  and and_30 (and_30_out, stepper_1_s4, and_21_out);
  and and_31 (and_31_out, stepper_1_s4, and_22_out);
  and and_32 (and_32_out, stepper_1_s4, IR[3], and_23_out);
  and C (C_out, IR[3], Carry_out);
  and A (A_out, IR[2], A_larger);
  and E (E_out, IR[1], Equal);
  and Z (Z_out, IR[0], zero);
  and and_33 (and_33_out, IR[12], IR[13], IR[14]);
  not not_2 (not_2_out, IR[3]);
  not not_3 (not_3_out, and_33_out);
  and and_34 (and_34_out, stepper_1_s5, IR[15]);
  and and_35 (and_35_out, stepper_1_s5, and_16_out);
  and and_36 (and_36_out, stepper_1_s5, and_17_out);
  and and_37 (and_37_out, stepper_1_s5, and_18_out);
  and and_38 (and_38_out, stepper_1_s5, and_20_out);
  and and_39 (and_39_out, stepper_1_s5, and_21_out);
  and and_40 (and_40_out, stepper_1_s5, and_23_out, not_2_out);
  or or_5 (or_5_out, C_out, A_out, E_out, Z_out);
  and and_41 (and_41_out, stepper_1_s6, IR[15], not_3_out);
  and and_42 (and_42_out, stepper_1_s6, and_18_out);
  and and_43 (and_43_out, stepper_1_s6, and_21_out, or_5_out);
  stepper stepper_1 (
    .clock(clk_1_enableclock), .init(init), .s1(stepper_1_s1), .s2(stepper_1_s2), .s3(stepper_1_s3),
    .s4(stepper_1_s4), .s5(stepper_1_s5), .s6(stepper_1_s6));
  or acc_s (acc_s_out, stepper_1_s1, and_27_out, and_30_out, and_34_out);
  or flags_s (flags_s_out, and_31_out, and_34_out);
  or reg_B_s (reg_B_s_out, and_35_out, and_41_out, and_37_out, and_40_out);
  Decoder #(.enable("false"), .select(2)) decoder_4 (
    .out0(decoder_4_out0), .out1(decoder_4_out1), .out2(decoder_4_out2), .out3(decoder_4_out3), .sel(IR[1:0]));
  or mar_s (mar_s_out, stepper_1_s1, and_27_out, and_30_out, and_25_out, and_26_out, and_29_out);
  or iar_s (iar_s_out, stepper_1_s3, and_28_out, and_38_out, and_39_out, and_42_out, and_43_out);
  and and_44 (IR_SET, clk_1_setclock, stepper_1_s2);
  and and_45 (MAR_SET, clk_1_setclock, mar_s_out);
  and and_46 (IAR_SET, clk_1_setclock, iar_s_out);
  and and_47 (ACC_SET, clk_1_setclock, acc_s_out);
  and and_48 (RAM_SET, clk_1_setclock, and_36_out);
  and and_49 (TMP_SET, clk_1_setclock, and_24_out);
  and and_50 (Flags_SET, clk_1_setclock, flags_s_out);
  and and_51 (I_O_clk_s, clk_1_setclock, and_32_out);
  and and_52 (R0_S, reg_B_s_out, clk_1_setclock, decoder_4_out0);
  and and_53 (R1_S, reg_B_s_out, clk_1_setclock, decoder_4_out1);
  and and_54 (R2_S, reg_B_s_out, clk_1_setclock, decoder_4_out2);
  and and_55 (R3_S, reg_B_s_out, clk_1_setclock, decoder_4_out3);

  assign Data_Address = IR[2];
  assign in_out_put = IR[3];
endmodule

module bus1 (
  input  [15:0] entrada,
  input  comando,
  output [15:0] saida
);

  Multiplexer #(.width(16)) multiplexer_1 (.in0(entrada), .in1(16'h1), .out(saida), .sel(comando));
endmodule

module stepper (
  input  clock,
  output init,
  output s1,
  output s2,
  output s3,
  output s4,
  output s5,
  output s6
);

  wire decoder_1_out7;
  wire [2:0] counter_1_q;

  Counter #(.max('h7), .width(3)) counter_1 (
    .D(3'b001), .Q(counter_1_q), .clk(clock), .clr(decoder_1_out7));  // open: load, count, carry, up
  Decoder #(.enable("false"), .select(3)) decoder_1 (
    .out0(init), .out1(s1), .out2(s2), .out3(s3), .out4(s4), .out5(s5), .out6(s6), .out7(decoder_1_out7),
    .sel(counter_1_q));
endmodule

module Flags (
  input  c_in,
  input  a_in,
  input  set_flags,
  input  e_in,
  input  z_in,
  output carry_out,
  output a_larger,
  output equal,
  output zero
);

  Register #(.width(4)) register_1 (
    .D({z_in, e_in, a_in, c_in}), .Q({zero, equal, a_larger, carry_out}), .clk(set_flags));  // open: en, clr
endmodule

module teclado (
  input  [15:0] in_1,
  input  input_ena,
  input  [6:0] in_3,
  input  input_set,
  input  data,
  input  i_o,
  output [15:0] out_7,
  output out_8,
  output out_9
);

  wire and_1_out, comparator_1_eq;
  wire [15:0] bit_extender_1_out;

  Comparator #(.width(16)) comparator_1 (.a(in_1), .b({16{1'b0}}), .eq(comparator_1_eq));  // open: gt, lt
  and and_1 (and_1_out, input_set, data, i_o);
  T_Flip_Flop t_ff_1 (.clk(input_ena), .T(1'b1), .Qn(out_8));  // open: Q, preset, reset
  Register #(.width(1)) register_1 (.D(comparator_1_eq), .Q(out_9), .clk(and_1_out));  // open: en, clr
  assign bit_extender_1_out = {{9{1'b0}}, in_3};  // Bit_Extender bit_extender_1
  assign out_7 = input_ena ? bit_extender_1_out : 16'bz;  // Controlled_Buffer controlled_buffer_1
endmodule

module monitor (
  input  [15:0] in_1,
  input  input_set,
  input  data,
  input  i_o,
  output [6:0] out_5,
  output out_6,
  output out_7
);

  wire and_1_out, comparator_1_eq;

  and and_1 (and_1_out, input_set, data, i_o);
  Bit_Extender #(.in_width(16), .out_width(7)) bit_extender_1 (.in(in_1), .out(out_5));
  Comparator #(.width(16)) comparator_1 (.a(in_1), .b(16'h1), .eq(comparator_1_eq));  // open: gt, lt
  Register #(.width(1)) register_1 (.D(comparator_1_eq), .Q(out_7), .clk(and_1_out));  // open: en, clr

  assign out_6 = input_set;
endmodule

module Porta_not (
  input  [15:0] in_1,
  output [15:0] out_2
);

  not not_1 (out_2[0], in_1[0]);
  not not_2 (out_2[1], in_1[1]);
  not not_3 (out_2[2], in_1[2]);
  not not_4 (out_2[3], in_1[3]);
  not not_5 (out_2[12], in_1[12]);
  not not_6 (out_2[13], in_1[13]);
  not not_7 (out_2[14], in_1[14]);
  not not_8 (out_2[15], in_1[15]);

  assign out_2[11:4] = in_1[11:4];
endmodule
